// Logisim project cpu.circ as structural Verilog: 4 circuits, main circuit main
module main (
  input  [31:0] INSTRUCTION,
  input  CLOCK,
  output [31:0] FETCH_ADDRESS,
  output [31:0] ra,
  output [31:0] sp,
  output [31:0] t0,
  output [31:0] t1,
  output [31:0] t2,
  output [31:0] s0,
  output [31:0] s1,
  output [31:0] a0
);

  wire ASel, BrEq, BrLT, BrUn, BSel, MemW, or_1_out, PCSel, Reg_WEn;
  wire [1:0] WBSel;
  wire [2:0] ImmSel;
  wire [3:0] alusel;
  wire [4:0] AddrA, AddrB, AddrD, bit_extender_1_out;
  wire [7:0] bit_extender_2_out;
  wire [15:0] bit_extender_3_out;
  wire [31:0] adder_1_out, alu_output, and_1_out, bit_extender_4_out, bit_extender_5_out, control_input,
       DataA, DataB, DataR, DataR_ROW, divider_2_out, ImmGen, multiplexer_1_out, multiplexer_4_out,
       multiplexer_5_out, multiplier_1_out, PC, PC_plus_4, PC_REAL, shifter_1_out, up_date, Write_Data;

  or or_1 (or_1_out, 1'b0, PCSel);
  Adder #(.width(32)) adder_1 (.a(PC), .b(32'h4), .out(adder_1_out));  // open: cin, cout
  Multiplexer #(.width(32), .enable("false")) multiplexer_1 (
    .in0(INSTRUCTION), .in1({32{1'b0}}), .out(multiplexer_1_out), .sel(or_1_out));
  Register #(.width(32)) IMEMD (
    .D(multiplexer_1_out), .clk(CLOCK),
    .Q({control_input[31:25], AddrB, AddrA, control_input[14:12], AddrD, control_input[6:0]}));  // open: en, clr
  Multiplexer #(.width(32), .enable("false")) multiplexer_2 (
    .in0(PC_plus_4), .in1(alu_output), .out(up_date), .sel(PCSel));
  Multiplexer #(.select(2), .width(32), .enable("false")) multiplexer_3 (
    .in0(adder_1_out), .in1(alu_output), .in2(DataR), .out(Write_Data), .sel(WBSel));  // open: in3
  Register #(.width(32)) register_1 (.D(up_date), .clk(CLOCK), .Q(PC_REAL));  // open: en, clr
  regfile_main main_1 (
    .Read_Register_1_rs1(AddrA), .Read_Register_2_rs2(AddrB), .Write_Register_rd(AddrD),
    .Write_Data(Write_Data), .Write_Enable(Reg_WEn), .Clock(CLOCK), .Read_Data_1(DataA), .Read_Data_2(DataB),
    .ra(ra), .sp(sp), .t0(t0), .t1(t1), .t2(t2), .s0(s0), .s1(s1), .a0(a0));
  Divider #(.width(32)) divider_1 (.a(PC_REAL), .b(32'h4), .out(FETCH_ADDRESS));  // open: upper, rem
  Adder #(.width(32)) adder_2 (.a(PC_REAL), .b(32'h4), .out(PC_plus_4));  // open: cin, cout
  Register #(.width(32)) PCD (.D(PC_REAL), .clk(CLOCK), .Q(PC));  // open: en, clr
  // Probe on {control_input[31:25], AddrB, AddrA, control_input[14:12], AddrD}
  Multiplexer #(.width(32), .enable("false")) multiplexer_4 (
    .in0(DataA), .in1(PC), .out(multiplexer_4_out), .sel(ASel));
  Multiplexer #(.width(32), .enable("false")) multiplexer_5 (
    .in0(DataB), .in1(ImmGen), .out(multiplexer_5_out), .sel(BSel));
  // Probe on alusel
  ImmGenerator immgenerator_1 (
    .immidiate_input({control_input[31:25], AddrB, AddrA, control_input[14:12], AddrD}),
    .ImmSel_input(ImmSel), .out_3(ImmGen));
  alu alu_1 (.A(multiplexer_4_out), .B(multiplexer_5_out), .ALUSel(alusel), .Result(alu_output));
  // Probe on s0
  assign and_1_out = alu_output & 32'h3;  // AND_Gate and_1, 32 bits wide
  Branch_Comp branch_comp_1 (.DataA(DataA), .DataB(DataB), .BrUn(BrUn), .BrLT(BrLT), .BrEq(BrEq));
  Control_Logic control_logic_1 (
    .BrEq(BrEq), .BrLT(BrLT),
    .Instruction({control_input[31:25], AddrB, AddrA, control_input[14:12], AddrD, control_input[6:0]}),
    .RegWEn(Reg_WEn), .ImmSel(ImmSel), .PCSel(PCSel), .BrUn(BrUn), .MemRW(MemW), .ASel(ASel),
    .ALUSel(alusel), .BSel(BSel), .WBSel(WBSel));
  Multiplier #(.width(32)) multiplier_1 (.a(and_1_out), .b(32'h8), .out(multiplier_1_out));  // open: cin, cout
  // Probe on a0
  Bit_Extender #(.in_width(32), .out_width(5)) bit_extender_1 (.in(multiplier_1_out), .out(bit_extender_1_out));
  Shifter #(.width(32), .shift("lr")) shifter_1 (.in(DataR_ROW), .\dist (bit_extender_1_out), .out(shifter_1_out));
  Divider #(.width(32)) divider_2 (.a(alu_output), .b(32'h4), .out(divider_2_out));  // open: upper, rem
  Bit_Extender #(.in_width(32), .out_width(8)) bit_extender_2 (.in(shifter_1_out), .out(bit_extender_2_out));
  Bit_Extender #(.in_width(32)) bit_extender_3 (.in(shifter_1_out), .out(bit_extender_3_out));
  // mem_main MEM: pin names not known; wires that end beside it: divider_2_out, DataB, MemW, CLOCK, DataR_ROW
  assign bit_extender_4_out = {{24{bit_extender_2_out[7]}}, bit_extender_2_out};  // Bit_Extender bit_extender_4
  assign bit_extender_5_out = {{16{bit_extender_3_out[15]}}, bit_extender_3_out};  // Bit_Extender bit_extender_5
  Multiplexer #(.select(2), .width(32), .enable("false")) multiplexer_6 (
    .in0(bit_extender_4_out), .in1(bit_extender_5_out), .in2(shifter_1_out), .out(DataR),
    .sel(control_input[13:12]));  // open: in3

  // Other names for the same wires on the sheet: clk = CLOCK;
  //   INSTRUCTION_EX[31:0] = {control_input[31:25], AddrB, AddrA, control_input[14:12], AddrD, control_input[6:0]};
  //   control_input (some bits) = {AddrB, AddrA, AddrD};
  //   imm_input[24:0] = {control_input[31:25], AddrB, AddrA, control_input[14:12], AddrD};
  //   fetch_addr[31:0] = FETCH_ADDRESS

  // Notes on the sheet:
  //   Output
  //   Inputs/Outputs from run.circ. DO NOT MOVE THESE.
  //   Inputs
  //   only have 4 bit
  //   Inputs/Outputs from run.circ. DO NOT MOVE THESE.
  //   It is OK to move the PC, RegFile, ALU, and MEM to wherever is most convenient for you when constructing your CPU, and to delete this text
endmodule

module ImmGenerator (
  input  [24:0] immidiate_input,
  input  [2:0] ImmSel_input,
  output [31:0] out_3
);

  wire [4:0] demultiplexer_1_out3, demultiplexer_1_out4;
  wire [11:0] adder_1_out, B_imm_out, I_imm_out, S_imm_out;
  wire [12:0] demultiplexer_1_out0;
  wire [17:5] demultiplexer_1_out1, demultiplexer_1_out2;
  wire [19:0] J_imm_out, u_imm_out;
  wire [31:0] adder_2_out, adder_3_out, bit_extender_1_out, bit_extender_2_out, bit_extender_3_out,
       bit_extender_4_out, shifter_1_out, shifter_2_out, shifter_3_out;

  Adder #(.width(12)) adder_1 (.a(S_imm_out), .b(I_imm_out), .out(adder_1_out));  // open: cin, cout
  // Probe on immidiate_input
  Demultiplexer #(.select(3), .width(25), .enable("false")) demultiplexer_1 (
    .out0({I_imm_out, demultiplexer_1_out0}), .out1({S_imm_out[11:5], demultiplexer_1_out1, S_imm_out[4:0]}),
    .out2({B_imm_out[11], B_imm_out[9:4], demultiplexer_1_out2, B_imm_out[3:0], B_imm_out[10]}),
    .out3({u_imm_out, demultiplexer_1_out3}),
    .out4({J_imm_out[19], J_imm_out[9:0], J_imm_out[10], J_imm_out[18:11], demultiplexer_1_out4}),
    .in(immidiate_input), .sel(ImmSel_input));  // open: out5, out6, out7
  // Probe on out_3
  assign bit_extender_1_out = {{20{adder_1_out[11]}}, adder_1_out};  // Bit_Extender bit_extender_1
  assign bit_extender_2_out = {{20{B_imm_out[11]}}, B_imm_out};  // Bit_Extender bit_extender_2
  assign bit_extender_3_out = {{12{1'b0}}, u_imm_out};  // Bit_Extender bit_extender_3
  assign bit_extender_4_out = {{12{J_imm_out[19]}}, J_imm_out};  // Bit_Extender bit_extender_4
  Shifter #(.width(32)) shifter_1 (.in(bit_extender_3_out), .\dist (5'b01100), .out(shifter_1_out));
  Shifter #(.width(32)) shifter_2 (.in(bit_extender_4_out), .\dist (5'b00001), .out(shifter_2_out));
  // Probe on I_imm_out
  // Probe on S_imm_out
  // Probe on J_imm_out
  Shifter #(.width(32)) shifter_3 (.in(bit_extender_2_out), .\dist (5'b00001), .out(shifter_3_out));
  Adder #(.width(32)) adder_2 (.a(bit_extender_1_out), .b(shifter_3_out), .out(adder_2_out));  // open: cin, cout
  Adder #(.width(32)) adder_3 (.a(shifter_1_out), .b(shifter_2_out), .out(adder_3_out));  // open: cin, cout
  Adder #(.width(32)) adder_4 (.a(adder_2_out), .b(adder_3_out), .out(out_3));  // open: cin, cout
endmodule

module Control_Logic (
  input  BrEq,
  input  BrLT,
  input  [31:0] Instruction,
  output RegWEn,
  output [2:0] ImmSel,
  output PCSel,
  output BrUn,
  output MemRW,
  output ASel,
  output [3:0] ALUSel,
  output BSel,
  output [1:0] WBSel
);

  wire and_1_out, and_2_out, and_3_out, and_4_out, and_6_out, and_8_out, and_9_out, and_10_out, and_11_out,
       and_12_out, and_13_out, and_14_out, and_15_out, and_16_out, and_17_out, and_18_out, and_19_out,
       and_20_out, and_21_out, and_22_out, and_23_out, and_24_out, comparator_9_eq, comparator_10_eq,
       comparator_11_eq, comparator_12_eq, comparator_13_eq, comparator_14_eq, comparator_15_eq,
       comparator_16_eq, comparator_17_eq, comparator_18_eq, comparator_20_eq, comparator_21_eq,
       comparator_22_eq, comparator_23_eq, comparator_24_eq, comparator_25_eq, comparator_26_eq,
       comparator_27_eq, comparator_28_eq, comparator_29_eq, comparator_30_eq, comparator_31_eq,
       comparator_32_eq, comparator_33_eq, comparator_34_eq, comparator_35_eq, comparator_36_eq,
       comparator_37_eq, comparator_38_eq, comparator_39_eq, comparator_40_eq, comparator_41_eq,
       comparator_42_eq, comparator_43_eq, comparator_44_eq, comparator_45_eq, comparator_46_eq, I_jalr,
       I_type, I_type_withload, multiplier_16_out, not_1_out, not_2_out, not_3_out, not_4_out, not_5_out,
       not_6_out, or_1_out, or_2_out, or_5_out, or_7_out, R_type, SB_PCSel, SB_type, U_type, UJ_type;
  wire [1:0] bit_extender_22_out, bit_extender_27_out, multiplier_21_out;
  wire [2:0] bit_extender_16_out, bit_extender_17_out, bit_extender_18_out, bit_extender_19_out,
       bit_extender_20_out, divider_1_rem, multiplier_17_out, multiplier_18_out, multiplier_19_out,
       multiplier_20_out;
  wire [3:0] add_output, adder_1_out, adder_2_out, adder_3_out, adder_4_out, adder_5_out, adder_6_out,
       adder_7_out, adder_8_out, adder_9_out, adder_10_out, adder_12_out, adder_14_out, adder_15_out,
       adder_16_out, adder_17_out, adder_18_out, and_output, andi_output, bit_extender_1_out,
       bit_extender_2_out, bit_extender_3_out, bit_extender_4_out, bit_extender_5_out, bit_extender_6_out,
       bit_extender_7_out, bit_extender_8_out, bit_extender_9_out, bit_extender_10_out, bit_extender_11_out,
       bit_extender_12_out, bit_extender_13_out, bit_extender_14_out, bit_extender_15_out,
       bit_extender_21_out, bit_extender_23_out, bit_extender_24_out, bit_extender_25_out,
       bit_extender_26_out, div_output, I_output, mul_output, mulh_output, or_output, ori_output, R_output,
       rem_output, sll_output, slli_output, slt_output, slti_output, srai_output, srl_output, srli_output,
       sub_output, U_output, xor_output, xori_output;

  Comparator #(.width(7), .mode("unsigned")) comparator_1 (
    .a(Instruction[6:0]), .b(7'b0110011), .eq(R_type));  // open: gt, lt
  Comparator #(.width(7), .mode("unsigned")) comparator_2 (
    .a(Instruction[6:0]), .b(7'b0000011), .eq(I_type_withload));  // open: gt, lt
  Comparator #(.width(7), .mode("unsigned")) comparator_3 (
    .a(Instruction[6:0]), .b(7'b0010011), .eq(I_type));  // open: gt, lt
  Comparator #(.width(7), .mode("unsigned")) comparator_4 (
    .a(Instruction[6:0]), .b(7'b0100011), .eq(MemRW));  // open: gt, lt
  Comparator #(.width(7), .mode("unsigned")) comparator_5 (
    .a(Instruction[6:0]), .b(7'b1100011), .eq(SB_type));  // open: gt, lt
  Comparator #(.width(7), .mode("unsigned")) comparator_6 (
    .a(Instruction[6:0]), .b(7'b0110111), .eq(U_type));  // open: gt, lt
  Comparator #(.width(7), .mode("unsigned")) comparator_7 (
    .a(Instruction[6:0]), .b(7'b1101111), .eq(UJ_type));  // open: gt, lt
  Comparator #(.width(7), .mode("unsigned")) comparator_8 (
    .a(Instruction[6:0]), .b(7'b1100111), .eq(I_jalr));  // open: gt, lt
  Comparator #(.width(3)) comparator_9 (.a(Instruction[14:12]), .b(3'b101), .eq(comparator_9_eq));  // open: gt, lt
  Comparator #(.width(7)) comparator_10 (.a(Instruction[31:25]), .b({7{1'b0}}), .eq(comparator_10_eq));  // open: gt, lt
  Adder #(.width(4)) adder_1 (.a(add_output), .b(mul_output), .out(adder_1_out));  // open: cin, cout
  Adder #(.width(4)) adder_2 (.a(sub_output), .b(sll_output), .out(adder_2_out));  // open: cin, cout
  Adder #(.width(4)) adder_3 (.a(mulh_output), .b(slt_output), .out(adder_3_out));  // open: cin, cout
  Adder #(.width(4)) adder_4 (.a(xor_output), .b(div_output), .out(adder_4_out));  // open: cin, cout
  Adder #(.width(4)) adder_5 (.a(srl_output), .b(or_output), .out(adder_5_out));  // open: cin, cout
  Adder #(.width(4)) adder_6 (.a(rem_output), .b(and_output), .out(adder_6_out));  // open: cin, cout
  Comparator #(.width(3)) comparator_11 (.a(Instruction[14:12]), .b(3'b101), .eq(comparator_11_eq));  // open: gt, lt
  Comparator #(.width(7)) comparator_12 (
    .a(Instruction[31:25]), .b(7'b0100000), .eq(comparator_12_eq));  // open: gt, lt
  Comparator #(.width(3)) comparator_13 (.a(Instruction[14:12]), .b(3'b010), .eq(comparator_13_eq));  // open: gt, lt
  and and_1 (and_1_out, I_type, comparator_9_eq, comparator_10_eq);
  Comparator #(.width(3)) comparator_14 (.a(Instruction[14:12]), .b(3'b001), .eq(comparator_14_eq));  // open: gt, lt
  Comparator #(.width(7)) comparator_15 (.a(Instruction[31:25]), .b({7{1'b0}}), .eq(comparator_15_eq));  // open: gt, lt
  not not_1 (not_1_out, R_type);
  not not_2 (not_2_out, I_type_withload);
  not not_3 (not_3_out, I_type);
  not not_4 (not_4_out, MemRW);
  not not_5 (not_5_out, U_type);
  or or_1 (or_1_out, UJ_type, I_jalr, SB_PCSel);
  Comparator #(.width(3), .mode("unsigned")) comparator_16 (
    .a(Instruction[14:12]), .b(3'b110), .eq(comparator_16_eq));  // open: gt, lt
  Comparator #(.width(3), .mode("unsigned")) comparator_17 (
    .a(Instruction[14:12]), .b(3'b000), .eq(comparator_17_eq));  // open: gt, lt
  Adder #(.width(4)) adder_7 (.a(adder_1_out), .b(adder_2_out), .out(adder_7_out));  // open: cin, cout
  Adder #(.width(4)) adder_8 (.a(adder_3_out), .b(adder_4_out), .out(adder_8_out));  // open: cin, cout
  Adder #(.width(4)) adder_9 (.a(adder_5_out), .b(adder_6_out), .out(adder_9_out));  // open: cin, cout
  and and_2 (and_2_out, I_type, comparator_11_eq, comparator_12_eq);
  and and_3 (and_3_out, I_type, comparator_13_eq);
  assign bit_extender_1_out = {{3{1'b0}}, and_1_out};  // Bit_Extender bit_extender_1
  and and_4 (and_4_out, I_type, comparator_14_eq, comparator_15_eq);
  and and_5 (BrUn, SB_type, comparator_16_eq);
  and and_6 (and_6_out, comparator_17_eq, BrEq);
  Comparator #(.width(3), .mode("unsigned")) comparator_18 (
    .a(Instruction[14:12]), .b(3'b001), .eq(comparator_18_eq));  // open: gt, lt
  not not_6 (not_6_out, BrEq);
  Adder #(.width(4)) adder_10 (.a(adder_7_out), .b(adder_8_out), .out(adder_10_out));  // open: cin, cout
  assign bit_extender_2_out = {{3{1'b0}}, U_type};  // Bit_Extender bit_extender_2
  assign bit_extender_3_out = {{3{1'b0}}, and_2_out};  // Bit_Extender bit_extender_3
  assign bit_extender_4_out = {{3{1'b0}}, and_3_out};  // Bit_Extender bit_extender_4
  assign bit_extender_5_out = {{3{1'b0}}, and_4_out};  // Bit_Extender bit_extender_5
  and and_7 (PCSel, not_1_out, not_2_out, not_3_out, not_4_out, not_5_out, or_1_out);
  and and_8 (and_8_out, SB_type, or_2_out);
  or or_2 (or_2_out, BrLT, and_6_out);
  and and_9 (and_9_out, comparator_18_eq, not_6_out);
  Adder #(.width(4)) adder_11 (.a(adder_10_out), .b(adder_9_out), .out(R_output));  // open: cin, cout
  Multiplier #(.width(4)) multiplier_1 (.a(bit_extender_2_out), .b(4'b1101), .out(U_output));  // open: cin, cout
  Multiplier #(.width(4)) multiplier_2 (.a(bit_extender_3_out), .b(4'b0101), .out(srai_output));  // open: cin, cout
  Multiplier #(.width(4)) multiplier_3 (.a(bit_extender_4_out), .b(4'b0111), .out(slti_output));  // open: cin, cout
  Multiplier #(.width(4)) multiplier_4 (.a(bit_extender_1_out), .b(4'b0100), .out(srli_output));  // open: cin, cout
  Multiplier #(.width(4)) multiplier_5 (.a(bit_extender_5_out), .b(4'b0110), .out(slli_output));  // open: cin, cout
  Divider #(.width(3)) divider_1 (.a(Instruction[14:12]), .b(3'b010), .rem(divider_1_rem));  // open: out, upper
  or or_3 (SB_PCSel, and_8_out, and_9_out);
  Adder #(.width(4)) adder_12 (.a(R_output), .b(U_output), .out(adder_12_out));  // open: cin, cout
  Comparator #(.width(3), .mode("unsigned")) comparator_19 (.a(divider_1_rem), .b(3'b000));  // open: gt, eq, lt
  Adder #(.width(4)) adder_13 (.a(adder_12_out), .b(I_output), .out(ALUSel));  // open: cin, cout
  Comparator #(.width(3)) comparator_20 (.a(Instruction[14:12]), .b(3'b100), .eq(comparator_20_eq));  // open: gt, lt
  Comparator #(.width(3)) comparator_21 (.a(Instruction[14:12]), .b(3'b110), .eq(comparator_21_eq));  // open: gt, lt
  Comparator #(.width(3)) comparator_22 (.a(Instruction[14:12]), .b(3'b111), .eq(comparator_22_eq));  // open: gt, lt
  and and_10 (and_10_out, I_type, comparator_20_eq);
  and and_11 (and_11_out, I_type, comparator_21_eq);
  and and_12 (and_12_out, I_type, comparator_22_eq);
  Adder #(.width(4)) adder_14 (.a(srai_output), .b(slti_output), .out(adder_14_out));  // open: cin, cout
  Adder #(.width(4)) adder_15 (.a(srli_output), .b(slli_output), .out(adder_15_out));  // open: cin, cout
  Adder #(.width(4)) adder_16 (.a(ori_output), .b(andi_output), .out(adder_16_out));  // open: cin, cout
  assign bit_extender_6_out = {{3{1'b0}}, and_10_out};  // Bit_Extender bit_extender_6
  assign bit_extender_7_out = {{3{1'b0}}, and_11_out};  // Bit_Extender bit_extender_7
  assign bit_extender_8_out = {{3{1'b0}}, and_12_out};  // Bit_Extender bit_extender_8
  Adder #(.width(4)) adder_17 (.a(adder_14_out), .b(adder_15_out), .out(adder_17_out));  // open: cin, cout
  Multiplier #(.width(4)) multiplier_6 (.a(bit_extender_6_out), .b(4'b0011), .out(xori_output));  // open: cin, cout
  Multiplier #(.width(4)) multiplier_7 (.a(bit_extender_7_out), .b(4'b0010), .out(ori_output));  // open: cin, cout
  Multiplier #(.width(4)) multiplier_8 (.a(bit_extender_8_out), .b(4'b0001), .out(andi_output));  // open: cin, cout
  Adder #(.width(4)) adder_18 (.a(adder_17_out), .b(adder_16_out), .out(adder_18_out));  // open: cin, cout
  or or_4 (RegWEn, R_type, I_type_withload, I_type, UJ_type, I_jalr, U_type);
  Comparator #(.width(3)) comparator_23 (.a(Instruction[14:12]), .b(3'b000), .eq(comparator_23_eq));  // open: gt, lt
  Comparator #(.width(7)) comparator_24 (.a(Instruction[31:25]), .b({7{1'b0}}), .eq(comparator_24_eq));  // open: gt, lt
  Comparator #(.width(3)) comparator_25 (.a(Instruction[14:12]), .b(3'b000), .eq(comparator_25_eq));  // open: gt, lt
  Comparator #(.width(7)) comparator_26 (
    .a(Instruction[31:25]), .b(7'b0000001), .eq(comparator_26_eq));  // open: gt, lt
  Comparator #(.width(3)) comparator_27 (.a(Instruction[14:12]), .b(3'b000), .eq(comparator_27_eq));  // open: gt, lt
  Comparator #(.width(7)) comparator_28 (
    .a(Instruction[31:25]), .b(7'b0100000), .eq(comparator_28_eq));  // open: gt, lt
  Comparator #(.width(3)) comparator_29 (.a(Instruction[14:12]), .b(3'b001), .eq(comparator_29_eq));  // open: gt, lt
  Comparator #(.width(7)) comparator_30 (.a(Instruction[31:25]), .b({7{1'b0}}), .eq(comparator_30_eq));  // open: gt, lt
  Comparator #(.width(3)) comparator_31 (.a(Instruction[14:12]), .b(3'b001), .eq(comparator_31_eq));  // open: gt, lt
  Comparator #(.width(7)) comparator_32 (
    .a(Instruction[31:25]), .b(7'b0000001), .eq(comparator_32_eq));  // open: gt, lt
  Comparator #(.width(3)) comparator_33 (.a(Instruction[14:12]), .b(3'b010), .eq(comparator_33_eq));  // open: gt, lt
  Comparator #(.width(7)) comparator_34 (.a(Instruction[31:25]), .b({7{1'b0}}), .eq(comparator_34_eq));  // open: gt, lt
  Comparator #(.width(3)) comparator_35 (.a(Instruction[14:12]), .b(3'b100), .eq(comparator_35_eq));  // open: gt, lt
  Comparator #(.width(7)) comparator_36 (.a(Instruction[31:25]), .b({7{1'b0}}), .eq(comparator_36_eq));  // open: gt, lt
  Adder #(.width(4)) adder_19 (.a(adder_18_out), .b(xori_output), .out(I_output));  // open: cin, cout
  and and_13 (and_13_out, R_type, comparator_23_eq, comparator_24_eq);
  and and_14 (and_14_out, R_type, comparator_25_eq, comparator_26_eq);
  and and_15 (and_15_out, R_type, comparator_27_eq, comparator_28_eq);
  and and_16 (and_16_out, R_type, comparator_29_eq, comparator_30_eq);
  and and_17 (and_17_out, R_type, comparator_31_eq, comparator_32_eq);
  and and_18 (and_18_out, R_type, comparator_33_eq, comparator_34_eq);
  and and_19 (and_19_out, R_type, comparator_35_eq, comparator_36_eq);
  assign bit_extender_9_out = {{3{1'b0}}, and_13_out};  // Bit_Extender bit_extender_9
  assign bit_extender_10_out = {{3{1'b0}}, and_14_out};  // Bit_Extender bit_extender_10
  assign bit_extender_11_out = {{3{1'b0}}, and_15_out};  // Bit_Extender bit_extender_11
  assign bit_extender_12_out = {{3{1'b0}}, and_16_out};  // Bit_Extender bit_extender_12
  assign bit_extender_13_out = {{3{1'b0}}, and_17_out};  // Bit_Extender bit_extender_13
  assign bit_extender_14_out = {{3{1'b0}}, and_18_out};  // Bit_Extender bit_extender_14
  assign bit_extender_15_out = {{3{1'b0}}, and_19_out};  // Bit_Extender bit_extender_15
  Multiplier #(.width(4)) multiplier_9 (.a(bit_extender_9_out), .b(4'b0000), .out(add_output));  // open: cin, cout
  Multiplier #(.width(4)) multiplier_10 (.a(bit_extender_10_out), .b(4'b1010), .out(mul_output));  // open: cin, cout
  Multiplier #(.width(4)) multiplier_11 (.a(bit_extender_11_out), .b(4'b1100), .out(sub_output));  // open: cin, cout
  Multiplier #(.width(4)) multiplier_12 (.a(bit_extender_12_out), .b(4'b0110), .out(sll_output));  // open: cin, cout
  Multiplier #(.width(4)) multiplier_13 (.a(bit_extender_13_out), .b(4'b1011), .out(mulh_output));  // open: cin, cout
  Multiplier #(.width(4)) multiplier_14 (.a(bit_extender_14_out), .b(4'b0111), .out(slt_output));  // open: cin, cout
  Multiplier #(.width(4)) multiplier_15 (.a(bit_extender_15_out), .b(4'b0011), .out(xor_output));  // open: cin, cout
  or or_5 (or_5_out, I_jalr, I_type_withload, I_type);
  assign bit_extender_16_out = {{2{1'b0}}, MemRW};  // Bit_Extender bit_extender_16
  assign bit_extender_17_out = {{2{1'b0}}, SB_type};  // Bit_Extender bit_extender_17
  assign bit_extender_18_out = {{2{1'b0}}, U_type};  // Bit_Extender bit_extender_18
  assign bit_extender_19_out = {{2{1'b0}}, UJ_type};  // Bit_Extender bit_extender_19
  assign bit_extender_20_out = {{2{1'b0}}, multiplier_16_out};  // Bit_Extender bit_extender_20
  Multiplier #(.width(1)) multiplier_16 (.a(or_5_out), .b(1'b0), .out(multiplier_16_out));  // open: cin, cout
  Multiplier #(.width(3)) multiplier_17 (
    .a(bit_extender_16_out), .b(3'b001), .out(multiplier_17_out));  // open: cin, cout
  Multiplier #(.width(3)) multiplier_18 (
    .a(bit_extender_17_out), .b(3'b010), .out(multiplier_18_out));  // open: cin, cout
  Multiplier #(.width(3)) multiplier_19 (
    .a(bit_extender_18_out), .b(3'b011), .out(multiplier_19_out));  // open: cin, cout
  Multiplier #(.width(3)) multiplier_20 (
    .a(bit_extender_19_out), .b(3'b100), .out(multiplier_20_out));  // open: cin, cout
  assign ImmSel = bit_extender_20_out | multiplier_17_out | multiplier_18_out | multiplier_19_out | multiplier_20_out;  // OR_Gate or_6, 3 bits wide
  Comparator #(.width(3)) comparator_37 (.a(Instruction[14:12]), .b(3'b111), .eq(comparator_37_eq));  // open: gt, lt
  Comparator #(.width(7)) comparator_38 (.a(Instruction[31:25]), .b({7{1'b0}}), .eq(comparator_38_eq));  // open: gt, lt
  Comparator #(.width(3)) comparator_39 (.a(Instruction[14:12]), .b(3'b100), .eq(comparator_39_eq));  // open: gt, lt
  Comparator #(.width(7)) comparator_40 (
    .a(Instruction[31:25]), .b(7'b0000001), .eq(comparator_40_eq));  // open: gt, lt
  Comparator #(.width(3)) comparator_41 (.a(Instruction[14:12]), .b(3'b101), .eq(comparator_41_eq));  // open: gt, lt
  Comparator #(.width(7)) comparator_42 (.a(Instruction[31:25]), .b({7{1'b0}}), .eq(comparator_42_eq));  // open: gt, lt
  Comparator #(.width(3)) comparator_43 (.a(Instruction[14:12]), .b(3'b110), .eq(comparator_43_eq));  // open: gt, lt
  Comparator #(.width(7)) comparator_44 (.a(Instruction[31:25]), .b({7{1'b0}}), .eq(comparator_44_eq));  // open: gt, lt
  Comparator #(.width(3)) comparator_45 (.a(Instruction[14:12]), .b(3'b110), .eq(comparator_45_eq));  // open: gt, lt
  Comparator #(.width(7)) comparator_46 (
    .a(Instruction[31:25]), .b(7'b0000001), .eq(comparator_46_eq));  // open: gt, lt
  and and_20 (and_20_out, R_type, comparator_39_eq, comparator_40_eq);
  and and_21 (and_21_out, R_type, comparator_41_eq, comparator_42_eq);
  and and_22 (and_22_out, R_type, comparator_43_eq, comparator_44_eq);
  and and_23 (and_23_out, R_type, comparator_45_eq, comparator_46_eq);
  assign bit_extender_21_out = {{3{1'b0}}, and_24_out};  // Bit_Extender bit_extender_21
  and and_24 (and_24_out, R_type, comparator_37_eq, comparator_38_eq);
  or or_7 (or_7_out, R_type, I_type, U_type);
  assign bit_extender_22_out = {{1{1'b0}}, I_type_withload};  // Bit_Extender bit_extender_22
  assign bit_extender_23_out = {{3{1'b0}}, and_20_out};  // Bit_Extender bit_extender_23
  assign bit_extender_24_out = {{3{1'b0}}, and_21_out};  // Bit_Extender bit_extender_24
  assign bit_extender_25_out = {{3{1'b0}}, and_22_out};  // Bit_Extender bit_extender_25
  assign bit_extender_26_out = {{3{1'b0}}, and_23_out};  // Bit_Extender bit_extender_26
  assign bit_extender_27_out = {{1{1'b0}}, or_7_out};  // Bit_Extender bit_extender_27
  Multiplier #(.width(2)) multiplier_21 (
    .a(bit_extender_22_out), .b(2'b10), .out(multiplier_21_out));  // open: cin, cout
  Multiplier #(.width(4)) multiplier_22 (.a(bit_extender_23_out), .b(4'b1000), .out(div_output));  // open: cin, cout
  Multiplier #(.width(4)) multiplier_23 (.a(bit_extender_24_out), .b(4'b0100), .out(srl_output));  // open: cin, cout
  Multiplier #(.width(4)) multiplier_24 (.a(bit_extender_25_out), .b(4'b0010), .out(or_output));  // open: cin, cout
  Multiplier #(.width(4)) multiplier_25 (.a(bit_extender_26_out), .b(4'b1001), .out(rem_output));  // open: cin, cout
  Multiplier #(.width(4)) multiplier_26 (.a(bit_extender_21_out), .b(4'b0001), .out(and_output));  // open: cin, cout
  assign WBSel = bit_extender_27_out | multiplier_21_out;  // OR_Gate or_8, 2 bits wide
  not not_7 (BSel, R_type);
  or or_9 (ASel, UJ_type, U_type, SB_type);

  // Other names for the same wires on the sheet: inst[31:0] = Instruction; opcode[6:0] = Instruction[6:0];
  //   funct3[2:0] = Instruction[14:12]; funct7[6:0] = Instruction[31:25]; S_type = MemRW
endmodule

module Branch_Comp (
  input  [31:0] DataA,
  input  [31:0] DataB,
  input  BrUn,
  output BrLT,
  output BrEq
);

  wire comparator_1_lt, comparator_2_lt;

  Comparator #(.width(32)) comparator_1 (.a(DataA), .b(DataB), .lt(comparator_1_lt));  // open: gt, eq
  Comparator #(.width(32), .mode("unsigned")) comparator_2 (
    .a(DataA), .b(DataB), .lt(comparator_2_lt));  // open: gt, eq
  Comparator #(.width(32)) comparator_3 (.a(DataA), .b(DataB), .eq(BrEq));  // open: gt, lt
  Multiplexer #(.enable("false")) multiplexer_1 (.in0(comparator_1_lt), .in1(comparator_2_lt), .out(BrLT), .sel(BrUn));

  // Other names for the same wires on the sheet: A[31:0] = DataA; B[31:0] = DataB; BrU = BrUn
endmodule
