// Logisim project regfile.circ as structural Verilog: 1 circuit, main circuit main
module main (
  input  [4:0] Read_Register_1_rs1,
  input  [4:0] Read_Register_2_rs2,
  input  [4:0] Write_Register_rd,
  input  [31:0] Write_Data,
  input  Write_Enable,
  input  Clock,
  output [31:0] ra,
  output [31:0] sp,
  output [31:0] t0,
  output [31:0] t1,
  output [31:0] t2,
  output [31:0] s0,
  output [31:0] s1,
  output [31:0] a0,
  output [31:0] Read_Data_1,
  output [31:0] Read_Data_2
);

  wire write_x1, write_x2, write_x5, write_x6, write_x7, write_x8, write_x9, write_x10;
  wire [31:0] x0_val;

  Multiplexer #(.select(5), .width(32), .enable("false")) multiplexer_1 (
    .in0(x0_val), .in1(ra), .in2(sp), .in5(t0), .in6(t1), .in7(t2), .in8(s0), .in9(s1), .in10(a0),
    .out(Read_Data_1), .sel(Read_Register_1_rs1));  // open: in3, in4, in11, in12, in13, in14, in15, in16, in17, in18, in19, in20, in21, in22, in23, in24, in25, in26, in27, in28, in29, in30, in31
  Multiplexer #(.select(5), .width(32), .enable("false")) multiplexer_2 (
    .in0(x0_val), .in1(ra), .in2(sp), .in5(t0), .in6(t1), .in7(t2), .in8(s0), .in9(s1), .in10(a0),
    .out(Read_Data_2), .sel(Read_Register_2_rs2));  // open: in3, in4, in11, in12, in13, in14, in15, in16, in17, in18, in19, in20, in21, in22, in23, in24, in25, in26, in27, in28, in29, in30, in31
  Register #(.width(32)) x1_ra (.D(Write_Data), .en(write_x1), .clk(Clock), .Q(ra));  // open: clr
  Register #(.width(32)) x5_t0 (.D(Write_Data), .en(write_x5), .clk(Clock), .Q(t0));  // open: clr
  Register #(.width(32)) x7_t2 (.D(Write_Data), .en(write_x7), .clk(Clock), .Q(t2));  // open: clr
  Register #(.width(32)) x9_s1 (.D(Write_Data), .en(write_x9), .clk(Clock), .Q(s1));  // open: clr
  Register #(.width(32)) x6_t1 (.D(Write_Data), .en(write_x6), .clk(Clock), .Q(t1));  // open: clr
  Register #(.width(32)) x8_s0 (.D(Write_Data), .en(write_x8), .clk(Clock), .Q(s0));  // open: clr
  Register #(.width(32)) x10_a0 (.D(Write_Data), .en(write_x10), .clk(Clock), .Q(a0));  // open: clr
  Register #(.width(32)) x2_sp (.D(Write_Data), .en(write_x2), .clk(Clock), .Q(sp));  // open: clr
  Demultiplexer #(.select(5), .enable("false")) demultiplexer_1 (
    .out1(write_x1), .out2(write_x2), .out5(write_x5), .out6(write_x6), .out7(write_x7), .out8(write_x8),
    .out9(write_x9), .out10(write_x10), .in(Write_Enable), .sel(Write_Register_rd));  // open: out0, out3, out4, out11, out12, out13, out14, out15, out16, out17, out18, out19, out20, out21, out22, out23, out24, out25, out26, out27, out28, out29, out30, out31
  Register #(.width(32)) x0 (.D({32{1'b0}}), .en(1'b1), .clk(Clock), .Q(x0_val));  // open: clr

  // Other names for the same wires on the sheet: clk = Clock; read_data1[31:0] = Read_Data_1;
  //   read_data2[31:0] = Read_Data_2; read_reg1[4:0] = Read_Register_1_rs1; read_reg2[4:0] = Read_Register_2_rs2;
  //   write_en = Write_Enable; write_reg[4:0] = Write_Register_rd

  // Notes on the sheet:
  //   INPUTS to your circuit
  //   DON'T CHANGE THE LOCATIONS OF THE INPUTS AND OUTPUTS!
  //   These are DEBUG/TEST outputs from your circuit.
  //   OUTPUTS from your circuit
endmodule
