// Logisim project alu.circ as structural Verilog: 2 circuits, main circuit alu
module alu (
  input  [31:0] A,
  input  [31:0] B,
  input  [3:0] ALUSel,
  output [31:0] Result
);

  wire comparator_1_lt;
  wire [31:0] add, b_and, b_or, b_sll, b_slt, b_sra, b_srl, b_xor, div, mul, mulh, remainder, sub;

  Adder #(.width(32)) adder_1 (.a(A), .b(B), .out(add));  // open: cin, cout
  Subtractor #(.width(32)) subtractor_1 (.a(A), .b(B), .out(sub));  // open: bin, bout
  Divider #(.width(32)) divider_1 (.a(A), .b(B), .out(div), .rem(remainder));  // open: upper
  Comparator #(.width(32)) comparator_1 (.a(A), .b(B), .lt(comparator_1_lt));  // open: gt, eq
  mulh_operator mulh_operator_1 (.Input_A(A), .Input_B(B), .mul_out(mul), .mulh_out(mulh));
  Shifter #(.width(32), .shift("lr")) shifter_1 (.in(A), .\dist (B[4:0]), .out(b_srl));
  Shifter #(.width(32), .shift("ar")) shifter_2 (.in(A), .\dist (B[4:0]), .out(b_sra));
  Shifter #(.width(32)) shifter_3 (.in(A), .\dist (B[4:0]), .out(b_sll));
  assign b_slt = {{31{1'b0}}, comparator_1_lt};  // Bit_Extender bit_extender_1
  assign b_xor = A ^ B;  // XOR_Gate xor_1, 32 bits wide
  assign b_or = A | B;  // OR_Gate or_1, 32 bits wide
  assign b_and = A & B;  // AND_Gate and_1, 32 bits wide
  Multiplexer #(.select(4), .width(32), .enable("false")) multiplexer_1 (
    .in0(add), .in1(b_and), .in2(b_or), .in3(b_xor), .in4(b_srl), .in5(b_sra), .in6(b_sll), .in7(b_slt),
    .in8(div), .in9(remainder), .in10(mul), .in11(mulh), .in12(sub), .in13(B), .out(Result), .sel(ALUSel));  // open: in14, in15

  // Other names for the same wires on the sheet: bsel[31:0] = B

  // Notes on the sheet:
  //   INPUTS to your circuit
  //   DON'T CHANGE THE LOCATIONS OF THE INPUTS AND OUTPUTS!
  //   1
  //   2
  //   3
  //   4
  //   5
  //   6
  //   7
  //   8
  //   9
  //   10
  //   11
  //   12
  //   13
  //   0
  //   OUTPUT from your circuit
endmodule

module mulh_operator (
  input  [31:0] Input_A,
  input  [31:0] Input_B,
  output [31:0] mul_out,
  output [31:0] mulh_out
);

  wire comparator_1_lt, comparator_2_lt;
  wire [1:0] comparator_3_lt;
  wire [31:0] A_negative, B_negative, mulh, multiplier_3_out, multiplier_4_out;

  Comparator #(.width(32)) comparator_1 (.a(Input_A), .b({32{1'b0}}), .lt(comparator_1_lt));  // open: gt, eq
  Comparator #(.width(32)) comparator_2 (.a(Input_B), .b({32{1'b0}}), .lt(comparator_2_lt));  // open: gt, eq
  Comparator #(.width(32)) comparator_3 (.a(Input_A), .b(Input_B), .lt(comparator_3_lt[0]));  // open: gt, eq
  xor xor_1 (comparator_3_lt[1], comparator_1_lt, comparator_2_lt);
  // Probe on multiplier_4_out
  // Probe on multiplier_3_out
  Multiplier #(.width(32)) multiplier_1 (.a(Input_A), .b(Input_B), .out(mul_out), .cout(mulh));  // open: cin
  Multiplier #(.width(32)) multiplier_2 (.a(Input_B), .b(Input_A), .out(mul_out), .cout(mulh));  // open: cin
  Multiplier #(.width(32)) multiplier_3 (.a({32{1'b1}}), .b(Input_A), .out(multiplier_3_out));  // open: cin, cout
  Multiplexer #(.select(2), .width(32), .enable("false")) multiplexer_1 (
    .in0(mulh), .in1(mulh), .in2(B_negative), .in3(A_negative), .out(mulh_out), .sel(comparator_3_lt));
  Multiplier #(.width(32)) multiplier_4 (.a({32{1'b1}}), .b(Input_B), .out(multiplier_4_out));  // open: cin, cout
  Adder #(.width(32)) adder_1 (.a(mulh), .b(multiplier_4_out), .out(A_negative));  // open: cin, cout
  // Probe on A_negative
  Adder #(.width(32)) adder_2 (.a(mulh), .b(multiplier_3_out), .out(B_negative));  // open: cin, cout
  // Probe on B_negative

  // Other names for the same wires on the sheet: A[31:0] = Input_A; B[31:0] = Input_B; mul[31:0] = mul_out;
  //   mul_o[31:0] = mulh_out
endmodule
